# Fritzing sketch tee_timer (saved by Fritzing 0.9.4)
breadboards: 1

parts:
  Bauteil1 = Arduino Nano (Rev3.0)
  J1 = Piezo Speaker
  DI1 = 7-Segment LED Display [package=THT]
  M1 = Dagu DGServo 9g (End View) [part_number=RS001B]
  R1 = Resistor [tolerance=±5% resistance=1k package="0402 [SMD]"]
  R2 = Resistor [tolerance=±5% resistance=1k package="0402 [SMD]"]
  R3 = Resistor [tolerance=±5% resistance=1k package="0402 [SMD]"]
  R4 = Resistor [tolerance=±5% resistance=1k package="0402 [SMD]"]
  R5 = Resistor [tolerance=±5% resistance=1k package="0402 [SMD]"]
  R6 = Resistor [tolerance=±5% resistance=1k package="0402 [SMD]"]
  R7 = Resistor [tolerance=±5% resistance=1k package="0402 [SMD]"]
  R9 = Resistor [tolerance=±5% resistance=1k package="0402 [SMD]"]
  R11 = Resistor [tolerance=±5% resistance=1k package="0402 [SMD]"]
  S1 = Pushbutton [package="[SMD]"]
  VCC1 = Battery block 9V

nets:
  GND: Bauteil1.GND, J1.pin1, DI1.commAnode, M1.gnd, R11.Pin_1
  N1: Bauteil1.D2, R5.Pin_1
  N2: Bauteil1.D3, R4.Pin_1
  N3: Bauteil1.D4, R2.Pin_1
  N4: Bauteil1.D5, R1.Pin_1
  N5: Bauteil1.D6, R9.Pin_1
  N6: Bauteil1.D7, R6.Pin_1
  N7: Bauteil1.D8, R7.Pin_1
  N8: Bauteil1.D9, R3.Pin_1
  N9: Bauteil1.D11/MOSI, J1.pin2
  N10: Bauteil1.D12/MISO, R11.Pin_0, S1.Pin_1, S1.Pin_2
  5V: Bauteil1.5V, M1.vcc, S1.Pin_3, S1.Pin_4, VCC1.-
  N11: DI1.cathodeE, R9.Pin_0
  N12: DI1.cathodeD, R1.Pin_0
  N13: DI1.cathodeC, R2.Pin_0
  N14: DI1.cathodeDP, R3.Pin_0
  N15: DI1.cathodeB, R4.Pin_0
  N16: DI1.cathodeA, R5.Pin_0
  N17: DI1.cathodeF, R6.Pin_0
  N18: DI1.cathodeG, R7.Pin_0
